// Logisim project real_Alu.circ as structural Verilog: 5 circuits, main circuit in_A and in_B
module in_A_and_in_B (
  input  [7:0] in_1,
  input  [7:0] in_2,
  output [7:0] out_3
);

  assign out_3 = in_1 & in_2;  // AND_Gate and_1, 8 bits wide
endmodule

module in_A_or_in_B (
  input  [7:0] in_1,
  input  [7:0] in_2,
  output [7:0] out_3
);

  assign out_3 = in_1 | in_2;  // OR_Gate or_1, 8 bits wide
endmodule

module not_in_B (
  input  [7:0] in_1,
  output [7:0] out_2
);

  assign out_2 = ~in_1;  // NOT_Gate not_1, 8 bits wide
endmodule

module LSL_in_b (
  input  [7:0] Num_b,
  output out_2,
  output [7:0] out_3
);


  assign out_2 = Num_b[7];
  assign out_3 = {Num_b[6:0], 1'b0};
endmodule

module LSR_in_b (
  input  [7:0] Num_b,
  output out_2,
  output [7:0] out_3
);


  assign out_2 = Num_b[0];
  assign out_3 = {1'b0, Num_b[7:1]};
endmodule
